# Fritzing sketch LED-Configuration-System (saved by Fritzing 0.9.4)
breadboards: 1

parts:
  Part1 = Arduino Uno (Rev3) - ICSP  # not connected
  LED1 = smd LED [color="Red (633nm)" package="0805 [SMD]"]
  R1 = Resistor [tolerance=±5% resistance=220 package="2010 [SMD]"]
  R2 = Resistor [tolerance=±5% resistance=220 package="0603 [SMD]"]
  LED2 = smd LED [color="Orange (620nm)" package="0603 [SMD]"]
  LED3 = LED - 5mm [color="Green (570nm)" package="5 mm [THT]"]
  R3 = Resistor [tolerance=±5% resistance=220 package="2010 [SMD]"]
  R4 = Resistor [tolerance=±5% resistance=220 package="2010 [SMD]"]
  S1 = Pushbutton [package="[THT]"]
  S2 = Pushbutton [package="[THT]"]
  S3 = Pushbutton [package="[THT]"]
  R5 = Resistor [tolerance=±5% resistance=220 package="0603 [SMD]"]
  R6 = Resistor [tolerance=±5% resistance=220 package="0603 [SMD]"]

nets:
  N1: LED1.cathode, R2.Pin_0, LED2.cathode, LED3.cathode, R5.Pin_0, R6.Pin_0
  N2: LED1.anode, R1.Pin_0, R1.Pin_1, LED2.anode, R3.Pin_0, R3.Pin_1, R4.Pin_0, S1.Pin_1, S1.Pin_2, S2.Pin_1, S2.Pin_2, S3.Pin_1, S3.Pin_2
  N3: R2.Pin_1, S1.Pin_3, S1.Pin_4
  N4: LED3.anode, R4.Pin_1
  N5: S2.Pin_3, S2.Pin_4, R5.Pin_1
  N6: S3.Pin_3, S3.Pin_4, R6.Pin_1
